// Logisim project simple_processor.circ as structural Verilog: 1 circuit, main circuit main
module main (
);

  wire and_1_out, and_2_out, and_3_out, and_4_out, CLK, decoder_1_out0, decoder_1_out1, decoder_1_out2,
       decoder_1_out3, demultiplexer_1_out0, demultiplexer_1_out1, demultiplexer_1_out2,
       demultiplexer_1_out3, EQ, GT, LT, NE, not_1_out, or_1_out, RegSel, WriteEn;
  wire [1:0] DestReg, Operation, SRC1;
  wire [7:0] adder_1_out, adder_2_out, and_5_out, Const, multiplexer_1_out, multiplexer_2_out,
       multiplexer_3_out, multiplexer_4_out, multiplexer_5_out, or_2_out, R0_q, R1_q, R2_q, R3_q,
       register_1_q, subtractor_1_out;

  Multiplexer #(.width(8)) multiplexer_1 (.in0(8'h1), .in1(Const), .out(multiplexer_1_out), .sel(or_1_out));
  // Probe on or_1_out
  and and_1 (and_1_out, EQ, decoder_1_out0);
  Register register_1 (.D(adder_1_out), .clk(CLK), .Q(register_1_q));  // open: en, clr
  Adder adder_1 (.a(multiplexer_1_out), .b(register_1_q), .out(adder_1_out));  // open: cin, cout
  or or_1 (or_1_out, and_1_out, and_2_out, and_3_out, and_4_out);
  and and_2 (and_2_out, NE, decoder_1_out1);
  and and_3 (and_3_out, LT, decoder_1_out2);
  Decoder #(.select(2)) decoder_1 (
    .out0(decoder_1_out0), .out1(decoder_1_out1), .out2(decoder_1_out2), .out3(decoder_1_out3),
    .sel(Operation), .en(not_1_out));
  not not_1 (not_1_out, WriteEn);
  // Probe on register_1_q
  and and_4 (and_4_out, GT, decoder_1_out3);
  ROM #(.dataWidth(16)) rom_1 (.addr(register_1_q), .data({WriteEn, Operation, RegSel, DestReg, SRC1, Const}));
  Clock clock_1 (.out(CLK));
  // Probe on {WriteEn, Operation, RegSel, DestReg, SRC1, Const}
  Demultiplexer #(.select(2)) demultiplexer_1 (
    .out0(demultiplexer_1_out0), .out1(demultiplexer_1_out1), .out2(demultiplexer_1_out2),
    .out3(demultiplexer_1_out3), .in(WriteEn), .sel(DestReg));
  // Probe on multiplexer_5_out
  Register R0 (.D(multiplexer_5_out), .en(demultiplexer_1_out0), .clk(CLK), .Q(R0_q));  // open: clr
  Register R1 (.D(multiplexer_5_out), .en(demultiplexer_1_out1), .clk(CLK), .Q(R1_q));  // open: clr
  Register R2 (.D(multiplexer_5_out), .en(demultiplexer_1_out2), .clk(CLK), .Q(R2_q));  // open: clr
  Register R3 (.D(multiplexer_5_out), .en(demultiplexer_1_out3), .clk(CLK), .Q(R3_q));  // open: clr
  // Probe on R0_q
  // Probe on R1_q
  // Probe on R2_q
  // Probe on R3_q
  // Probe on SRC1
  // Probe on Const[1:0]
  Multiplexer #(.select(2), .width(8)) multiplexer_2 (
    .in0(R0_q), .in1(R1_q), .in2(R2_q), .in3(R3_q), .out(multiplexer_2_out), .sel(SRC1));
  Multiplexer #(.select(2), .width(8)) multiplexer_3 (
    .in0(R0_q), .in1(R1_q), .in2(R2_q), .in3(R3_q), .out(multiplexer_3_out), .sel(Const[1:0]));
  not not_2 (NE, EQ);
  Comparator comparator_1 (.a(multiplexer_2_out), .b({8{1'b0}}), .gt(GT), .eq(EQ), .lt(LT));
  Multiplexer #(.width(8)) multiplexer_4 (.in0(Const), .in1(multiplexer_3_out), .out(multiplexer_4_out), .sel(RegSel));
  // Probe on multiplexer_2_out
  // Probe on multiplexer_4_out
  Adder adder_2 (.a(multiplexer_2_out), .b(multiplexer_4_out), .out(adder_2_out));  // open: cin, cout
  Subtractor subtractor_1 (.a(multiplexer_2_out), .b(multiplexer_4_out), .out(subtractor_1_out));  // open: bin, bout
  assign and_5_out = multiplexer_2_out & multiplexer_4_out;  // AND_Gate and_5, 8 bits wide
  assign or_2_out = multiplexer_2_out | multiplexer_4_out;  // OR_Gate or_2, 8 bits wide
  Multiplexer #(.select(2), .width(8)) multiplexer_5 (
    .in0(adder_2_out), .in1(subtractor_1_out), .in2(and_5_out), .in3(or_2_out), .out(multiplexer_5_out),
    .sel(Operation));
  // Probe on multiplexer_5_out

  // Other names for the same wires on the sheet: SRC2[1:0] = Const[1:0]

  // Notes on the sheet:
  //   Will you jump (branch)?
  //   Logic whether to branch out or not.
  //   WriteEn = 0 corresponds to branch instruction
  //   Go to address of next instruction logic
  //   Address of current instruction
  //   Instruction Fetch
  //   The clock signal. Click me to run the processor.
  //   Instruction memory
  //   Demux for data writes
  //   Current instruction
  //   Instruction partitioning
  //   Simplified processor (16-bit instructions, 8-bit data, 4 registers, 4 operations, 4 branch conditions, Immediate support)
  //   Instruction Decode
  //   The four 8-bit registers: R0, R1, R2, R3
  //   Data to write
  //   Mux for data reads
  //   Mux for data reads
  //   Compare vs 0
  //   Output of the operation (ADD/SUB/AND/OR) going back to the registers for writing
  //   Branch condition checks
  //   Register/constant selector
  //   First operand
  //   Second operand
  //   Instruction Execute
  //   Four operations
  //   Operation selector
endmodule
